// Logisim project Circuito refeito, simples organizado.circ as structural Verilog: 5 circuits, main circuit main
module main (
  input  Complementar_B,
  input  Complementar_A,
  input  chave__0_soma__1_sub,
  input  [5:0] A,
  input  [5:0] B
);

  wire c0, c1, c2, c3, c4, s_minus, s_plus, sA_minus, sA_plus, \Saída , \Saída_minus , \Saída_plus ,
       sB_minus, sB_plus, som_sub_6_bits_1_overflow;
  wire [5:5] Result;

  _7_Segment_Display u_7_segment_display_1 (.g(sA_minus), .b(sA_plus), .c(sA_plus));  // open: f, a, e, d, dp
  _7_Segment_Display u_7_segment_display_2 (.g(sA_plus), .f(sA_plus), .e(sA_plus));  // open: a, b, d, c, dp
  Hex_Digit_Display hex_digit_display_1 (.value({2'b00, A[5:4]}));  // open: dp
  Hex_Digit_Display hex_digit_display_2 (.value(A[3:0]));  // open: dp
  _7_Segment_Display u_7_segment_display_3 (.g(s_minus), .b(s_plus), .c(s_plus));  // open: f, a, e, d, dp
  _7_Segment_Display u_7_segment_display_4 (.g(s_plus), .f(s_plus), .e(s_plus));  // open: a, b, d, c, dp
  SOM_SUB_6_bits som_sub_6_bits_1 (
    .A(A), .B(B), .m(chave__0_soma__1_sub), .out_6({Result[5], c4, c3, c2, c1, c0}),
    .Overflow(som_sub_6_bits_1_overflow), .c2a(Complementar_A), .c2b(Complementar_B), .Saida(\Saída ));
  LED OVERFLOW (.in(som_sub_6_bits_1_overflow));
  _7_Segment_Display u_7_segment_display_5 (.g(sB_minus), .b(sB_plus), .c(sB_plus));  // open: f, a, e, d, dp
  _7_Segment_Display u_7_segment_display_6 (.g(sB_plus), .f(sB_plus), .e(sB_plus));  // open: a, b, d, c, dp
  Hex_Digit_Display hex_digit_display_3 (.value({2'b00, B[5:4]}));  // open: dp
  Hex_Digit_Display hex_digit_display_4 (.value(B[3:0]));  // open: dp
  _7_Segment_Display u_7_segment_display_7 (
    .g(\Saída_minus ), .b(\Saída_plus ), .c(\Saída_plus ));  // open: f, a, e, d, dp
  _7_Segment_Display u_7_segment_display_8 (
    .g(\Saída_plus ), .f(\Saída_plus ), .e(\Saída_plus ));  // open: a, b, d, c, dp
  Hex_Digit_Display hex_digit_display_5 (.value({3'b000, c4}));  // open: dp
  Hex_Digit_Display hex_digit_display_6 (.value({c3, c2, c1, c0}));  // open: dp
  or or_1 (s_minus, chave__0_soma__1_sub, 1'b1);
  xnor xnor_1 (s_plus, chave__0_soma__1_sub, 1'b0);
  not not_1 (\Saída_plus , \Saída );
  or or_2 (\Saída_minus , \Saída , 1'b1);
  xnor xnor_2 (sA_plus, Complementar_A, 1'b0);
  xnor xnor_3 (sB_plus, Complementar_B, 1'b0);
  or or_3 (sA_minus, Complementar_A, 1'b1);
  or or_4 (sB_minus, Complementar_B, 1'b1);

  // Other names for the same wires on the sheet: cpmA = Complementar_A; cpmB = Complementar_B;
  //   Result[4:0] = {c4, c3, c2, c1, c0}; Sinal_op = chave__0_soma__1_sub

  // Notes on the sheet:
  //   entrada B
  //   =
  //   saída
  //   negativo op
  //   positivo op
  //   sinais operação
  //   saída negativa
  //   saída positiva
  //   sinais saida
  //   sinais A
  //   negativo a
  //   positivo a
  //   sinais B
  //   negativo b
  //   positivo b
endmodule

module Somador_subtrator (
  input  A,
  input  B,
  input  Te,
  input  M,
  output S,
  output Ts
);

  wire and_1_out, and_2_out, or_1_out, xor_1_out, xor_2_out;

  xor xor_1 (xor_1_out, A, B);
  and and_1 (and_1_out, Te, B);
  xor xor_2 (xor_2_out, M, A);
  or or_1 (or_1_out, B, Te);
  and and_2 (and_2_out, xor_2_out, or_1_out);
  xor xor_3 (S, xor_1_out, Te);
  or or_2 (Ts, and_1_out, and_2_out);
endmodule

module C2 (
  input  chave,
  input  [5:0] entrada,
  output [5:0] complemento_de_2
);

  wire somador_1_ts, somador_2_ts, somador_3_ts, somador_4_ts, somador_5_ts, somador_6_s;
  wire [4:0] xor_6_out;

  Somador somador_1 (.A(xor_6_out[0]), .B(chave), .Te(1'b0), .S(complemento_de_2[0]), .Ts(somador_1_ts));
  Somador somador_2 (.A(xor_6_out[1]), .B(1'b0), .Te(somador_1_ts), .S(complemento_de_2[1]), .Ts(somador_2_ts));
  Somador somador_3 (.A(xor_6_out[2]), .B(1'b0), .Te(somador_2_ts), .S(complemento_de_2[2]), .Ts(somador_3_ts));
  Somador somador_4 (.A(xor_6_out[3]), .B(1'b0), .Te(somador_3_ts), .S(complemento_de_2[3]), .Ts(somador_4_ts));
  Somador somador_5 (.A(xor_6_out[4]), .B(1'b0), .Te(somador_4_ts), .S(complemento_de_2[4]), .Ts(somador_5_ts));
  Somador somador_6 (.A(entrada[5]), .B(1'b0), .Te(somador_5_ts), .S(somador_6_s));  // open: Ts
  xor xor_1 (complemento_de_2[5], somador_6_s, chave);
  xor xor_2 (xor_6_out[3], entrada[3], chave);
  xor xor_3 (xor_6_out[4], entrada[4], chave);
  xor xor_4 (xor_6_out[1], entrada[1], chave);
  xor xor_5 (xor_6_out[2], entrada[2], chave);
  xor xor_6 (xor_6_out[0], entrada[0], chave);

  // Other names for the same wires on the sheet: a = chave; t0 = entrada[0]; t1 = entrada[1]; t2 = entrada[2];
  //   t3 = entrada[3]; t4 = entrada[4]

  // Notes on the sheet:
  //   entrada
  //   selecao tirar ou nao complemento de 2
  //   saída
endmodule

module Somador (
  input  A,
  input  B,
  input  Te,
  output S,
  output Ts
);

  wire and_1_out, and_2_out, and_3_out, xor_1_out;

  xor xor_1 (xor_1_out, A, B);
  and and_1 (and_1_out, B, Te);
  and and_2 (and_2_out, Te, A);
  and and_3 (and_3_out, A, B);
  xor xor_2 (S, xor_1_out, Te);
  or or_1 (Ts, and_1_out, and_2_out, and_3_out);
endmodule

module SOM_SUB_6_bits (
  input  c2a,
  input  c2b,
  input  [5:0] A,
  input  [5:0] B,
  input  m,
  output [5:0] out_6,
  output Overflow,
  output Saida
);

  wire _0_ts, _1_ts, _2_ts, _3_ts, a0, a1, a2, a3, a4, a5, b0, b1, b2, b3, b4, b5, nor_1_out, overnegativo,
       s0, s1, s2, s3, s4, Te, Ts, xor_1_out;

  C2 c2_1 (.entrada(A), .chave(c2a), .complemento_de_2({a5, a4, a3, a2, a1, a0}));
  Somador_subtrator _0 (.A(a0), .B(b0), .Te(1'b0), .M(m), .S(s0), .Ts(_0_ts));
  Somador_subtrator _1 (.A(a1), .B(b1), .Te(_0_ts), .M(m), .S(s1), .Ts(_1_ts));
  Somador_subtrator _2 (.A(a2), .B(b2), .Te(_1_ts), .M(m), .S(s2), .Ts(_2_ts));
  Somador_subtrator _3 (.A(a3), .B(b3), .Te(_2_ts), .M(m), .S(s3), .Ts(_3_ts));
  Somador_subtrator _4 (.A(a4), .B(b4), .Te(_3_ts), .M(m), .S(s4), .Ts(Te));
  Somador_subtrator _5 (.A(a5), .B(b5), .Te(Te), .M(m), .S(Saida), .Ts(Ts));
  C2 c2_2 (.entrada(B), .chave(c2b), .complemento_de_2({b5, b4, b3, b2, b1, b0}));
  C2 c2_3 (.entrada({Saida, s4, s3, s2, s1, s0}), .chave(Saida), .complemento_de_2(out_6));
  xor xor_1 (xor_1_out, Te, Ts);
  nor nor_1 (nor_1_out, out_6[0], out_6[1], out_6[2], out_6[3], out_6[4]);
  or or_1 (Overflow, xor_1_out, overnegativo);
  and and_1 (overnegativo, nor_1_out, out_6[5]);

  // Other names for the same wires on the sheet: s5 = Saida

  // Notes on the sheet:
  //   -
  //   sinal
  //   Verificação de overflow negativo
  //   Verificação overflow
endmodule
