// Logisim project Somador subtrator funcionando.circ as structural Verilog: 2 circuits, main circuit somadorsubtrator
module somadorsubtrator (
  input  A,
  input  B,
  input  Te,
  input  M,
  output S,
  output Ts
);

  wire and_1_out, and_2_out, or_1_out, xor_1_out, xor_2_out;

  xor xor_1 (xor_1_out, A, B);
  and and_1 (and_1_out, Te, B);
  xor xor_2 (xor_2_out, M, A);
  or or_1 (or_1_out, B, Te);
  and and_2 (and_2_out, xor_2_out, or_1_out);
  xor xor_3 (S, xor_1_out, Te);
  or or_2 (Ts, and_1_out, and_2_out);
endmodule

module somador2bits (
  input  in_1,
  input  [2:0] A,
  input  [2:0] B,
  output out_4,
  output out_5,
  output out_6,
  output out_7
);

  wire somadorsubtrator_1_ts, somadorsubtrator_2_ts;

  somadorsubtrator somadorsubtrator_1 (.A(A[0]), .B(B[0]), .Te(in_1), .M(in_1), .S(out_4), .Ts(somadorsubtrator_1_ts));
  somadorsubtrator somadorsubtrator_2 (
    .A(A[1]), .B(B[1]), .Te(somadorsubtrator_1_ts), .M(in_1), .S(out_5), .Ts(somadorsubtrator_2_ts));
  somadorsubtrator somadorsubtrator_3 (.A(A[2]), .B(B[2]), .Te(somadorsubtrator_2_ts), .M(in_1), .S(out_6), .Ts(out_7));
endmodule
