// Logisim project TRABALHO TESTE.circ as structural Verilog: 3 circuits, main circuit main
module main (
  input  A,
  input  B,
  input  Te,
  input  M,
  output S,
  output Ts
);

  wire and_1_out, and_2_out, or_1_out, xor_1_out, xor_2_out;

  xor xor_1 (xor_1_out, A, B);
  and and_1 (and_1_out, Te, B);
  xor xor_2 (xor_2_out, M, A);
  or or_1 (or_1_out, B, Te);
  and and_2 (and_2_out, xor_2_out, or_1_out);
  xor xor_3 (S, xor_1_out, Te);
  or or_2 (Ts, and_1_out, and_2_out);
endmodule

module somador4BITS (
  input  in_1,
  input  A,
  input  B,
  input  A1,
  input  B_2,
  input  A2,
  input  B_3,
  input  A3,
  input  B_4,
  output out_10,
  output out_11,
  output out_12,
  output out_13,
  output out_14
);

  wire fulladder_1_ts, fulladder_2_ts, fulladder_3_ts, xor_1_out, xor_2_out, xor_3_out, xor_4_out;

  xor xor_1 (xor_1_out, B, in_1);
  xor xor_2 (xor_2_out, B_2, in_1);
  xor xor_3 (xor_3_out, B_3, in_1);
  xor xor_4 (xor_4_out, B_4, in_1);
  FULLADDER fulladder_1 (.Te(in_1), .A(A), .B(xor_1_out), .S(out_10), .Ts(fulladder_1_ts));
  FULLADDER fulladder_2 (.Te(fulladder_1_ts), .A(A1), .B(xor_2_out), .S(out_11), .Ts(fulladder_2_ts));
  FULLADDER fulladder_3 (.Te(fulladder_2_ts), .A(A2), .B(xor_3_out), .S(out_12), .Ts(fulladder_3_ts));
  FULLADDER fulladder_4 (.Te(fulladder_3_ts), .A(A3), .B(xor_4_out), .S(out_13), .Ts(out_14));
endmodule

module FULLADDER (
  input  Te,
  input  A,
  input  B,
  output S,
  output Ts
);

  wire and_1_out, and_2_out, and_3_out, xor_1_out;

  xor xor_1 (xor_1_out, A, B);
  and and_1 (and_1_out, B, Te);
  and and_2 (and_2_out, Te, A);
  and and_3 (and_3_out, A, B);
  xor xor_2 (S, Te, xor_1_out);
  or or_1 (Ts, and_1_out, and_2_out, and_3_out);
endmodule
