// Logisim project Trabalho - Copia.circ as structural Verilog: 6 circuits, main circuit main
module main (
  input  [5:0] A,
  input  \Chave_operação ,
  input  [5:0] B,
  output OVER
);

  wire _0_ts, _1_ts, _3_ts, _4_ts, _5_ts, somador_subtrador_1_ts, undriven;
  wire [3:0] _0_s, _4_s;

  xor xor_1 (OVER, _4_ts, _5_ts);
  somador_subtrador _5 (.A(A[5]), .B(B[5]), .Te(_4_ts), .M(\Chave_operação ), .S(_4_s[1]), .Ts(_5_ts));
  Hex_Digit_Display hex_digit_display_1 (.value({{2{_4_s[3]}}, _4_s[1:0]}), .dp(undriven));
  somador_subtrador _4 (.A(A[4]), .B(B[4]), .Te(_3_ts), .M(\Chave_operação ), .S(_4_s[0]), .Ts(_4_ts));
  somador_subtrador _3 (.A(A[3]), .B(B[3]), .Te(somador_subtrador_1_ts), .M(\Chave_operação ), .S(_0_s[3]), .Ts(_3_ts));
  somador_subtrador somador_subtrador_1 (
    .A(A[2]), .B(B[2]), .Te(_1_ts), .M(\Chave_operação ), .S(_0_s[2]), .Ts(somador_subtrador_1_ts));
  somador_subtrador _1 (.A(A[1]), .B(B[1]), .Te(_0_ts), .M(\Chave_operação ), .S(_0_s[1]), .Ts(_1_ts));
  Hex_Digit_Display hex_digit_display_2 (.value(_0_s), .dp(undriven));
  somador_subtrador _0 (.A(A[0]), .B(B[0]), .Te(\Chave_operação ), .M(\Chave_operação ), .S(_0_s[0]), .Ts(_0_ts));

  // Notes on the sheet:
  //   2
endmodule

module meiosomador (
  input  [1:0] AB,
  output s,
  output Ts
);

  xor xor_1 (s, AB[0], AB[1]);
  and and_1 (Ts, AB[0], AB[1]);
endmodule

module fulladder (
  input  A,
  input  B,
  input  Te,
  output S,
  output Ts
);

  wire and_1_out, and_2_out, and_3_out, xor_1_out;

  xor xor_1 (xor_1_out, A, B);
  and and_1 (and_1_out, B, Te);
  and and_2 (and_2_out, Te, A);
  and and_3 (and_3_out, A, B);
  xor xor_2 (S, xor_1_out, Te);
  or or_1 (Ts, and_1_out, and_2_out, and_3_out);
endmodule

module somador_subtrador (
  input  A,
  input  B,
  input  Te,
  input  M,
  output S,
  output Ts
);

  wire and_1_out, and_2_out, or_1_out, xor_1_out, xor_2_out;

  xor xor_1 (xor_1_out, A, B);
  and and_1 (and_1_out, Te, B);
  xor xor_2 (xor_2_out, M, A);
  or or_1 (or_1_out, B, Te);
  and and_2 (and_2_out, xor_2_out, or_1_out);
  xor xor_3 (S, xor_1_out, Te);
  or or_2 (Ts, and_1_out, and_2_out);
endmodule

module soma_sub_overflow (
  input  A,
  input  B,
  input  Te,
  input  M,
  output S
);

  wire and_1_out, and_2_out, or_1_out, or_2_out, xor_1_out, xor_2_out, xor_4_out;

  xor xor_1 (xor_1_out, A, B);
  and and_1 (and_1_out, Te, B);
  xor xor_2 (xor_2_out, M, A);
  or or_1 (or_1_out, B, Te);
  and and_2 (and_2_out, xor_2_out, or_1_out);
  xor xor_3 (S, xor_1_out, Te);
  or or_2 (or_2_out, and_1_out, and_2_out);
  xor xor_4 (xor_4_out, or_2_out, Te);
  LED overflow (.in(xor_4_out));
endmodule

module soma_sub_6_bits (
  input  in_1,
  input  in_2,
  input  [5:0] A,
  input  [5:0] B,
  input  chave
);

  wire soma_sub_overflow_1_s, somador_subtrador_1_ts, somador_subtrador_2_ts, somador_subtrador_3_ts,
       somador_subtrador_4_ts;

  LED led_1 (.in(soma_sub_overflow_1_s));
  somador_subtrador somador_subtrador_1 (
    .A(A[0]), .B(B[0]), .Te(chave), .M(chave), .Ts(somador_subtrador_1_ts));  // open: S
  somador_subtrador somador_subtrador_2 (
    .A(A[1]), .B(B[1]), .Te(somador_subtrador_1_ts), .M(chave), .Ts(somador_subtrador_2_ts));  // open: S
  somador_subtrador somador_subtrador_3 (
    .A(A[2]), .B(B[2]), .Te(somador_subtrador_2_ts), .M(chave), .Ts(somador_subtrador_3_ts));  // open: S
  somador_subtrador somador_subtrador_4 (
    .A(A[3]), .B(B[3]), .Te(somador_subtrador_3_ts), .M(chave), .Ts(somador_subtrador_4_ts));  // open: S
  soma_sub_overflow soma_sub_overflow_1 (
    .A(A[4]), .B(B[4]), .Te(somador_subtrador_4_ts), .M(chave), .S(soma_sub_overflow_1_s));
  Hex_Digit_Display hex_digit_display_1 (.value({{3{in_2}}, A[4]}));  // open: dp
  Hex_Digit_Display hex_digit_display_2 (.value({{2{A[2]}}, A[1:0]}));  // open: dp
  Hex_Digit_Display hex_digit_display_3 (.value({{3{in_1}}, B[4]}));  // open: dp
  Hex_Digit_Display hex_digit_display_4 (.value(B[3:0]));  // open: dp
endmodule
