// Logisim project Trabalho.circ as structural Verilog: 4 circuits, main circuit main
module main (
  input  [5:0] A,
  input  in_2,
  input  [5:0] B,
  output OVER
);

  wire _0_ts, _1_ts, somador_subtrador_1_ts;
  wire [3:0] _0_s, _4_s;

  xor xor_1 (OVER, B[4], _4_s[1]);
  Hex_Digit_Display hex_digit_display_1 (.value({{2{_4_s[3]}}, _4_s[1:0]}));  // open: dp
  somador_subtrador _4 (.A(A[4]), .B(B[4]), .Te(B[4]), .M(in_2), .S(_4_s[0]), .Ts(_4_s[1]));
  somador_subtrador _3 (.A(A[3]), .B(B[3]), .Te(somador_subtrador_1_ts), .M(in_2), .S(_0_s[3]), .Ts(B[4]));
  somador_subtrador somador_subtrador_1 (
    .A(A[2]), .B(B[2]), .Te(_1_ts), .M(in_2), .S(_0_s[2]), .Ts(somador_subtrador_1_ts));
  somador_subtrador _1 (.A(A[1]), .B(B[1]), .Te(_0_ts), .M(in_2), .S(_0_s[1]), .Ts(_1_ts));
  Hex_Digit_Display hex_digit_display_2 (.value(_0_s));  // open: dp
  somador_subtrador _0 (.A(A[0]), .B(B[0]), .Te(in_2), .M(in_2), .S(_0_s[0]), .Ts(_0_ts));

  // Notes on the sheet:
  //   2
endmodule

module meiosomador (
  input  [1:0] AB,
  output s,
  output Ts
);

  xor xor_1 (s, AB[0], AB[1]);
  and and_1 (Ts, AB[0], AB[1]);
endmodule

module fulladder (
  input  A,
  input  B,
  input  Te,
  output S,
  output Ts
);

  wire and_1_out, and_2_out, and_3_out, xor_1_out;

  xor xor_1 (xor_1_out, A, B);
  and and_1 (and_1_out, B, Te);
  and and_2 (and_2_out, Te, A);
  and and_3 (and_3_out, A, B);
  xor xor_2 (S, xor_1_out, Te);
  or or_1 (Ts, and_1_out, and_2_out, and_3_out);
endmodule

module somador_subtrador (
  input  A,
  input  B,
  input  Te,
  input  M,
  output S,
  output Ts
);

  wire and_1_out, and_2_out, or_1_out, xor_1_out, xor_2_out;

  xor xor_1 (xor_1_out, A, B);
  and and_1 (and_1_out, Te, B);
  xor xor_2 (xor_2_out, M, A);
  or or_1 (or_1_out, B, Te);
  and and_2 (and_2_out, xor_2_out, or_1_out);
  xor xor_3 (S, xor_1_out, Te);
  or or_2 (Ts, and_1_out, and_2_out);
endmodule
