// Logisim project circuito certo backup versão 10.circ as structural Verilog: 9 circuits, main circuit main
module main (
  input  [5:0] A,
  input  \Chave_operação ,
  input  [5:0] B,
  output OVER
);

  wire _0_ts, _1_ts, _3_ts, _4_ts, _5_ts, somador_subtrador_1_ts, undriven;
  wire [3:0] _0_s, _4_s;

  xor xor_1 (OVER, _4_ts, _5_ts);
  somador_subtrador _5 (.A(A[5]), .B(B[5]), .Te(_4_ts), .M(\Chave_operação ), .S(_4_s[1]), .Ts(_5_ts));
  Hex_Digit_Display hex_digit_display_1 (.value({{2{_4_s[3]}}, _4_s[1:0]}), .dp(undriven));
  somador_subtrador _4 (.A(A[4]), .B(B[4]), .Te(_3_ts), .M(\Chave_operação ), .S(_4_s[0]), .Ts(_4_ts));
  somador_subtrador _3 (.A(A[3]), .B(B[3]), .Te(somador_subtrador_1_ts), .M(\Chave_operação ), .S(_0_s[3]), .Ts(_3_ts));
  somador_subtrador somador_subtrador_1 (
    .A(A[2]), .B(B[2]), .Te(_1_ts), .M(\Chave_operação ), .S(_0_s[2]), .Ts(somador_subtrador_1_ts));
  somador_subtrador _1 (.A(A[1]), .B(B[1]), .Te(_0_ts), .M(\Chave_operação ), .S(_0_s[1]), .Ts(_1_ts));
  Hex_Digit_Display hex_digit_display_2 (.value(_0_s), .dp(undriven));
  somador_subtrador _0 (.A(A[0]), .B(B[0]), .Te(\Chave_operação ), .M(\Chave_operação ), .S(_0_s[0]), .Ts(_0_ts));

  // Notes on the sheet:
  //   2
endmodule

module meiosomador (
  input  A,
  input  B,
  output s,
  output Ts
);

  xor xor_1 (s, A, B);
  and and_1 (Ts, A, B);
endmodule

module fulladder (
  input  A,
  input  B,
  input  Te,
  output S,
  output Ts
);

  wire and_1_out, and_2_out, and_3_out, xor_1_out;

  xor xor_1 (xor_1_out, A, B);
  and and_1 (and_1_out, B, Te);
  and and_2 (and_2_out, Te, A);
  and and_3 (and_3_out, A, B);
  xor xor_2 (S, xor_1_out, Te);
  or or_1 (Ts, and_1_out, and_2_out, and_3_out);
endmodule

module somador_subtrador (
  input  A,
  input  B,
  input  Te,
  input  M,
  output S,
  output Ts
);

  wire and_1_out, and_2_out, or_1_out, xor_1_out, xor_2_out;

  xor xor_1 (xor_1_out, A, B);
  and and_1 (and_1_out, Te, B);
  xor xor_2 (xor_2_out, M, A);
  or or_1 (or_1_out, B, Te);
  and and_2 (and_2_out, xor_2_out, or_1_out);
  xor xor_3 (S, xor_1_out, Te);
  or or_2 (Ts, and_1_out, and_2_out);
endmodule

module soma_sub_overflow (
  input  A,
  input  B,
  input  Te,
  input  M,
  output S
);

  wire and_1_out, and_2_out, or_1_out, or_2_out, xor_1_out, xor_2_out, xor_4_out;

  xor xor_1 (xor_1_out, A, B);
  and and_1 (and_1_out, Te, B);
  xor xor_2 (xor_2_out, M, A);
  or or_1 (or_1_out, B, Te);
  and and_2 (and_2_out, xor_2_out, or_1_out);
  xor xor_3 (S, xor_1_out, Te);
  or or_2 (or_2_out, and_1_out, and_2_out);
  xor xor_4 (xor_4_out, or_2_out, Te);
  LED overflow (.in(xor_4_out));
endmodule

module soma_sub_6_bits (
  input  Complementar_B,
  input  Complementar_A,
  input  chave__0_soma__1_sub,
  input  [5:0] A,
  input  [5:0] B,
  input  in_6
);

  wire _0_ts, _1_ts, _2_ts, a5, and_2_out, b5, c0, c1, c2, c3, c4, c5, complemento2_2_lsb,
       complemento2_2_out_4, complemento2_2_out_5, complemento2_2_out_6, complemento2_2_out_7,
       complemento2_3_lsb, complemento2_3_out_4, complemento2_3_out_5, complemento2_3_out_6,
       complemento2_3_out_7, nor_1_out, OVERFLOW, overnegativo, s0, s1, s2, s3, s4, s5, s_minus, s_plus,
       sA_minus, sA_plus, \Saída_minus , \Saída_plus , sB_minus, sB_plus, somador_subtrador_1_ts, Ts, Ts4,
       xor_1_out;

  Complemento2 complemento2_1 (
    .entrada({s5, s4, s3, s2, s1, s0}), .MSB(c5), .Cpl(s5), .out_7(c4), .out_6(c3), .out_5(c2), .out_4(c1),
    .LSB(c0));  // open: Ts
  somador_subtrador _0 (
    .A(complemento2_2_lsb), .B(complemento2_3_lsb), .Te(and_2_out), .M(chave__0_soma__1_sub), .S(s0),
    .Ts(_0_ts));
  somador_subtrador _1 (
    .A(complemento2_2_out_4), .B(complemento2_3_out_4), .Te(_0_ts), .M(chave__0_soma__1_sub), .S(s1),
    .Ts(_1_ts));
  somador_subtrador _2 (
    .A(complemento2_2_out_5), .B(complemento2_3_out_5), .Te(_1_ts), .M(chave__0_soma__1_sub), .S(s2),
    .Ts(_2_ts));
  somador_subtrador somador_subtrador_1 (
    .A(complemento2_2_out_6), .B(complemento2_3_out_6), .Te(_2_ts), .M(chave__0_soma__1_sub), .S(s3),
    .Ts(somador_subtrador_1_ts));
  somador_subtrador somador_subtrador_2 (
    .A(complemento2_2_out_7), .B(complemento2_3_out_7), .Te(somador_subtrador_1_ts),
    .M(chave__0_soma__1_sub), .S(s4), .Ts(Ts4));
  somador_subtrador somador_subtrador_3 (.A(a5), .B(b5), .Te(Ts4), .M(chave__0_soma__1_sub), .S(s5), .Ts(Ts));
  Complemento2 complemento2_2 (
    .entrada(A), .MSB(a5), .Cpl(Complementar_A), .out_7(complemento2_2_out_7), .out_6(complemento2_2_out_6),
    .out_5(complemento2_2_out_5), .out_4(complemento2_2_out_4), .LSB(complemento2_2_lsb));  // open: Ts
  and and_1 (overnegativo, c5, nor_1_out);
  nor nor_1 (nor_1_out, c0, c1, c2, c3, c4);
  Complemento2 complemento2_3 (
    .entrada(B), .MSB(b5), .Cpl(Complementar_B), .out_7(complemento2_3_out_7), .out_6(complemento2_3_out_6),
    .out_5(complemento2_3_out_5), .out_4(complemento2_3_out_4), .LSB(complemento2_3_lsb));  // open: Ts
  and and_2 (and_2_out, in_6, chave__0_soma__1_sub);
  xor xor_1 (xor_1_out, Ts, Ts4);
  LED led_1 (.in(OVERFLOW));
  or or_1 (OVERFLOW, xor_1_out, overnegativo);
  _7_Segment_Display u_7_segment_display_1 (.g(sA_minus), .b(sA_plus), .c(sA_plus));  // open: f, a, e, d, dp
  _7_Segment_Display u_7_segment_display_2 (.g(sA_plus), .f(sA_plus), .e(sA_plus));  // open: a, b, d, c, dp
  _7_Segment_Display u_7_segment_display_3 (
    .g(\Saída_minus ), .b(\Saída_plus ), .c(\Saída_plus ));  // open: f, a, e, d, dp
  Hex_Digit_Display hex_digit_display_1 (.value(A[3:0]));  // open: dp
  Hex_Digit_Display hex_digit_display_2 (.value({2'b00, A[5:4]}));  // open: dp
  _7_Segment_Display u_7_segment_display_4 (
    .g(\Saída_plus ), .f(\Saída_plus ), .e(\Saída_plus ));  // open: a, b, d, c, dp
  Hex_Digit_Display hex_digit_display_3 (.value({3'b000, c4}));  // open: dp
  Hex_Digit_Display hex_digit_display_4 (.value({c3, c2, c1, c0}));  // open: dp
  not not_1 (\Saída_plus , s5);
  or or_2 (\Saída_minus , s5, 1'b1);
  _7_Segment_Display u_7_segment_display_5 (.g(s_plus), .f(s_plus), .e(s_plus));  // open: a, b, d, c, dp
  _7_Segment_Display u_7_segment_display_6 (.g(s_minus), .b(s_plus), .c(s_plus));  // open: f, a, e, d, dp
  _7_Segment_Display u_7_segment_display_7 (.g(sB_minus), .b(sB_plus), .c(sB_plus));  // open: f, a, e, d, dp
  _7_Segment_Display u_7_segment_display_8 (.g(sB_plus), .f(sB_plus), .e(sB_plus));  // open: a, b, d, c, dp
  Hex_Digit_Display hex_digit_display_5 (.value({2'b00, B[5:4]}));  // open: dp
  Hex_Digit_Display hex_digit_display_6 (.value(B[3:0]));  // open: dp
  xnor xnor_1 (s_plus, chave__0_soma__1_sub, 1'b0);
  or or_3 (s_minus, chave__0_soma__1_sub, 1'b1);
  xnor xnor_2 (sA_plus, Complementar_A, 1'b0);
  xnor xnor_3 (sB_plus, Complementar_B, 1'b0);
  or or_4 (sA_minus, Complementar_A, 1'b1);
  or or_5 (sB_minus, Complementar_B, 1'b1);

  // Other names for the same wires on the sheet: Saída = s5; cpmA = Complementar_A; Sa = Complementar_A;
  //   cpmB = Complementar_B; Sb = Complementar_B; Sinal_op = chave__0_soma__1_sub

  // Notes on the sheet:
  //   3
  //   4
  //   verificação de Overflow
  //   =
  //   entrada A
  //   saída
  //   saída negativa
  //   saída positiva
  //   operação
  //   entrada B
  //   sinais operação
  //   negativo op
  //   positivo op
  //   sinais A
  //   negativo a
  //   positivo a
  //   sinais B
  //   negativo b
  //   positivo b
endmodule

module complemento_de_2 (
  input  [5:0] entrada,
  input  in_2,
  output [5:0] complemento_de_2,
  output [5:0] normal
);

  wire fulladder_1_ts, fulladder_2_ts, fulladder_3_ts, fulladder_4_ts, fulladder_5_ts, fulladder_6_s;
  wire [4:0] not_4_out;

  fulladder fulladder_1 (.A(not_4_out[0]), .B(1'b1), .Te(in_2), .S(complemento_de_2[0]), .Ts(fulladder_1_ts));
  fulladder fulladder_2 (.A(not_4_out[1]), .B(in_2), .Te(fulladder_1_ts), .S(complemento_de_2[1]), .Ts(fulladder_2_ts));
  fulladder fulladder_3 (.A(not_4_out[2]), .B(in_2), .Te(fulladder_2_ts), .S(complemento_de_2[2]), .Ts(fulladder_3_ts));
  fulladder fulladder_4 (.A(not_4_out[3]), .B(in_2), .Te(fulladder_3_ts), .S(complemento_de_2[3]), .Ts(fulladder_4_ts));
  fulladder fulladder_5 (.A(not_4_out[4]), .B(in_2), .Te(fulladder_4_ts), .S(complemento_de_2[4]), .Ts(fulladder_5_ts));
  fulladder fulladder_6 (.A(entrada[5]), .B(in_2), .Te(fulladder_5_ts), .S(fulladder_6_s));  // open: Ts
  not not_1 (not_4_out[3], entrada[3]);
  not not_2 (not_4_out[4], entrada[4]);
  not not_3 (complemento_de_2[5], fulladder_6_s);
  not not_4 (not_4_out[0], entrada[0]);
  not not_5 (not_4_out[2], entrada[2]);
  not not_6 (not_4_out[1], entrada[1]);
  not not_7 (normal[1], complemento_de_2[1]);
  not not_8 (normal[2], complemento_de_2[2]);
  not not_9 (normal[3], complemento_de_2[3]);
  not not_10 (normal[4], complemento_de_2[4]);
  not not_11 (normal[5], complemento_de_2[5]);

  assign normal[0] = complemento_de_2[0];

  // Notes on the sheet:
  //   entrada
  //   saída
endmodule

module Complemento2 (
  input  [5:0] entrada,
  input  Cpl,
  output Ts,
  output out_4,
  output out_5,
  output out_6,
  output out_7,
  output MSB,
  output LSB
);

  wire meiosomador_1_ts, meiosomador_2_ts, meiosomador_3_ts, meiosomador_4_ts, meiosomador_5_ts, xor_1_out,
       xor_2_out, xor_3_out, xor_4_out, xor_5_out, xor_6_out;

  xor xor_1 (xor_1_out, Cpl, entrada[0]);
  meiosomador meiosomador_1 (.A(xor_1_out), .B(Cpl), .s(LSB), .Ts(meiosomador_1_ts));
  xor xor_2 (xor_2_out, Cpl, entrada[1]);
  meiosomador meiosomador_2 (.A(xor_2_out), .B(meiosomador_1_ts), .s(out_4), .Ts(meiosomador_2_ts));
  xor xor_3 (xor_3_out, Cpl, entrada[2]);
  meiosomador meiosomador_3 (.A(xor_3_out), .B(meiosomador_2_ts), .s(out_5), .Ts(meiosomador_3_ts));
  xor xor_4 (xor_4_out, Cpl, entrada[3]);
  meiosomador meiosomador_4 (.A(xor_4_out), .B(meiosomador_3_ts), .s(out_6), .Ts(meiosomador_4_ts));
  xor xor_5 (xor_5_out, Cpl, entrada[4]);
  meiosomador meiosomador_5 (.A(xor_5_out), .B(meiosomador_4_ts), .s(out_7), .Ts(meiosomador_5_ts));
  xor xor_6 (xor_6_out, Cpl, entrada[5]);
  meiosomador meiosomador_6 (.A(xor_6_out), .B(meiosomador_5_ts), .s(MSB), .Ts(Ts));
  _7_Segment_Display u_7_segment_display_1 (.g(MSB));  // open: f, a, b, e, d, c, dp
  Hex_Digit_Display hex_digit_display_1 (.value({2'b00, entrada[5:4]}));  // open: dp
  Hex_Digit_Display hex_digit_display_2 (.value(entrada[3:0]));  // open: dp

  // Other names for the same wires on the sheet: display0cpl[3:0] = entrada[3:0]; display1cpl[1:0] = entrada[5:4]
endmodule

module teste_c2 (
  input  [5:0] in_1,
  input  in_2,
  output out_3,
  output out_4,
  output out_5,
  output out_6,
  output out_7,
  output out_8
);

  Complemento2 complemento2_1 (
    .entrada(in_1), .MSB(out_8), .Cpl(in_2), .out_7(out_7), .out_6(out_6), .out_5(out_5), .out_4(out_4),
    .LSB(out_3));  // open: Ts
endmodule
