// Logisim project circuito certo backup.circ as structural Verilog: 9 circuits, main circuit main
module main (
  input  [5:0] A,
  input  \Chave_operação ,
  input  [5:0] B,
  output OVER
);

  wire _0_ts, _1_ts, _3_ts, _4_ts, _5_ts, somador_subtrador_1_ts, undriven;
  wire [3:0] _0_s, _4_s;

  xor xor_1 (OVER, _4_ts, _5_ts);
  somador_subtrador _5 (.A(A[5]), .B(B[5]), .Te(_4_ts), .M(\Chave_operação ), .S(_4_s[1]), .Ts(_5_ts));
  Hex_Digit_Display hex_digit_display_1 (.value({{2{_4_s[3]}}, _4_s[1:0]}), .dp(undriven));
  somador_subtrador _4 (.A(A[4]), .B(B[4]), .Te(_3_ts), .M(\Chave_operação ), .S(_4_s[0]), .Ts(_4_ts));
  somador_subtrador _3 (.A(A[3]), .B(B[3]), .Te(somador_subtrador_1_ts), .M(\Chave_operação ), .S(_0_s[3]), .Ts(_3_ts));
  somador_subtrador somador_subtrador_1 (
    .A(A[2]), .B(B[2]), .Te(_1_ts), .M(\Chave_operação ), .S(_0_s[2]), .Ts(somador_subtrador_1_ts));
  somador_subtrador _1 (.A(A[1]), .B(B[1]), .Te(_0_ts), .M(\Chave_operação ), .S(_0_s[1]), .Ts(_1_ts));
  Hex_Digit_Display hex_digit_display_2 (.value(_0_s), .dp(undriven));
  somador_subtrador _0 (.A(A[0]), .B(B[0]), .Te(\Chave_operação ), .M(\Chave_operação ), .S(_0_s[0]), .Ts(_0_ts));

  // Notes on the sheet:
  //   2
endmodule

module meiosomador (
  input  A,
  input  B,
  output s,
  output Ts
);

  xor xor_1 (s, A, B);
  and and_1 (Ts, A, B);
endmodule

module fulladder (
  input  A,
  input  B,
  input  Te,
  output S,
  output Ts
);

  wire and_1_out, and_2_out, and_3_out, xor_1_out;

  xor xor_1 (xor_1_out, A, B);
  and and_1 (and_1_out, B, Te);
  and and_2 (and_2_out, Te, A);
  and and_3 (and_3_out, A, B);
  xor xor_2 (S, xor_1_out, Te);
  or or_1 (Ts, and_1_out, and_2_out, and_3_out);
endmodule

module somador_subtrador (
  input  A,
  input  B,
  input  Te,
  input  M,
  output S,
  output Ts
);

  wire and_1_out, and_2_out, or_1_out, xor_1_out, xor_2_out;

  xor xor_1 (xor_1_out, A, B);
  and and_1 (and_1_out, Te, B);
  xor xor_2 (xor_2_out, M, A);
  or or_1 (or_1_out, B, Te);
  and and_2 (and_2_out, xor_2_out, or_1_out);
  xor xor_3 (S, xor_1_out, Te);
  or or_2 (Ts, and_1_out, and_2_out);
endmodule

module soma_sub_overflow (
  input  A,
  input  B,
  input  Te,
  input  M,
  output S
);

  wire and_1_out, and_2_out, or_1_out, or_2_out, xor_1_out, xor_2_out, xor_4_out;

  xor xor_1 (xor_1_out, A, B);
  and and_1 (and_1_out, Te, B);
  xor xor_2 (xor_2_out, M, A);
  or or_1 (or_1_out, B, Te);
  and and_2 (and_2_out, xor_2_out, or_1_out);
  xor xor_3 (S, xor_1_out, Te);
  or or_2 (or_2_out, and_1_out, and_2_out);
  xor xor_4 (xor_4_out, or_2_out, Te);
  LED overflow (.in(xor_4_out));
endmodule

module soma_sub_6_bits (
  input  [5:0] A,
  input  in_2,
  input  cpmB,
  input  [5:0] B,
  input  cpmA,
  input  in_6,
  input  \chave_0_soma__1subtração 
);

  wire _0_ts, _1_ts, _2_ts, _5_s, and_1_out, complemento2_2_lsb, complemento2_2_msb, complemento2_2_out_4,
       complemento2_2_out_5, complemento2_2_out_6, complemento2_2_out_7, somador_subtrador_1_ts,
       somador_subtrador_2_ts;
  wire [0:0] somador_subtrador_2_s;
  wire [1:0] complemento2_1_out_7, undriven;
  wire [3:0] _0_s, complemento2_1_lsb, undriven_2;

  Hex_Digit_Display hex_digit_display_1 (.value({3'b000, somador_subtrador_2_s[0]}));  // open: dp
  Hex_Digit_Display hex_digit_display_2 (.value(_0_s));  // open: dp
  LED led_1 (.in(_5_s));
  somador_subtrador _0 (
    .A(complemento2_1_lsb[0]), .B(complemento2_2_lsb), .Te(and_1_out), .M(\chave_0_soma__1subtração ),
    .S(_0_s[0]), .Ts(_0_ts));
  somador_subtrador _1 (
    .A(complemento2_1_lsb[1]), .B(complemento2_2_out_4), .Te(_0_ts), .M(\chave_0_soma__1subtração ),
    .S(_0_s[1]), .Ts(_1_ts));
  somador_subtrador _2 (
    .A(complemento2_1_lsb[2]), .B(complemento2_2_out_5), .Te(_1_ts), .M(\chave_0_soma__1subtração ),
    .S(_0_s[2]), .Ts(_2_ts));
  somador_subtrador somador_subtrador_1 (
    .A(complemento2_1_lsb[3]), .B(complemento2_2_out_6), .Te(_2_ts), .M(\chave_0_soma__1subtração ),
    .S(_0_s[3]), .Ts(somador_subtrador_1_ts));
  somador_subtrador somador_subtrador_2 (
    .A(complemento2_1_out_7[0]), .B(complemento2_2_out_7), .Te(somador_subtrador_1_ts),
    .M(\chave_0_soma__1subtração ), .S(somador_subtrador_2_s[0]), .Ts(somador_subtrador_2_ts));
  soma_sub_overflow _5 (
    .A(complemento2_1_out_7[1]), .B(complemento2_2_msb), .Te(somador_subtrador_2_ts),
    .M(\chave_0_soma__1subtração ), .S(_5_s));
  Complemento2 complemento2_1 (
    .entrada(A), .MSB(complemento2_1_out_7[1]), .Cpl(cpmA), .out_7(complemento2_1_out_7[0]),
    .out_6(complemento2_1_lsb[3]), .out_5(complemento2_1_lsb[2]), .out_4(complemento2_1_lsb[1]),
    .LSB(complemento2_1_lsb[0]));  // open: Ts
  _7_Segment_Display u_7_segment_display_1 (.g(cpmA));  // open: f, a, b, e, d, c, dp
  Hex_Digit_Display hex_digit_display_3 (.value({2'b00, complemento2_1_out_7}));  // open: dp
  Hex_Digit_Display hex_digit_display_4 (.value(complemento2_1_lsb));  // open: dp
  Complemento2 complemento2_2 (
    .entrada(B), .MSB(complemento2_2_msb), .Cpl(cpmB), .out_7(complemento2_2_out_7),
    .out_6(complemento2_2_out_6), .out_5(complemento2_2_out_5), .out_4(complemento2_2_out_4),
    .LSB(complemento2_2_lsb));  // open: Ts
  and and_1 (and_1_out, in_6, \chave_0_soma__1subtração );
  Hex_Digit_Display hex_digit_display_5 (.value({{2{in_2}}, undriven}));  // open: dp
  Hex_Digit_Display hex_digit_display_6 (.value(undriven_2));  // open: dp
  // Probe on nothing

  // Other names for the same wires on the sheet: Sa = cpmA

  // Notes on the sheet:
  //   =
  //   saída
  //   3
  //   4
  //   entrada A
  //   entrada B
endmodule

module complemento_de_2 (
  input  in_1,
  input  [5:0] entrada,
  input  in_3,
  output [5:0] complemento_de_2
);

  wire fulladder_1_ts, fulladder_2_ts, fulladder_3_ts, fulladder_4_ts, fulladder_5_ts, fulladder_6_s,
       not_1_out, xnor_2_out, xnor_3_out, xnor_4_out, xnor_5_out, xnor_6_out;
  wire [4:0] not_6_out;

  fulladder fulladder_1 (.A(not_6_out[0]), .B(in_1), .Te(in_3), .S(complemento_de_2[0]), .Ts(fulladder_1_ts));
  fulladder fulladder_2 (.A(not_6_out[1]), .B(in_3), .Te(fulladder_1_ts), .S(complemento_de_2[1]), .Ts(fulladder_2_ts));
  fulladder fulladder_3 (.A(not_6_out[2]), .B(in_3), .Te(fulladder_2_ts), .S(complemento_de_2[2]), .Ts(fulladder_3_ts));
  fulladder fulladder_4 (.A(not_6_out[3]), .B(in_3), .Te(fulladder_3_ts), .S(complemento_de_2[3]), .Ts(fulladder_4_ts));
  fulladder fulladder_5 (.A(not_6_out[4]), .B(in_3), .Te(fulladder_4_ts), .S(complemento_de_2[4]), .Ts(fulladder_5_ts));
  fulladder fulladder_6 (.A(entrada[5]), .B(in_3), .Te(fulladder_5_ts), .S(fulladder_6_s));  // open: Ts
  not not_1 (not_1_out, fulladder_6_s);
  xnor xnor_1 (complemento_de_2[5], not_1_out, in_1);
  xnor xnor_2 (xnor_2_out, entrada[3], in_1);
  xnor xnor_3 (xnor_3_out, entrada[4], in_1);
  not not_2 (not_6_out[3], xnor_2_out);
  not not_3 (not_6_out[4], xnor_3_out);
  xnor xnor_4 (xnor_4_out, entrada[2], in_1);
  xnor xnor_5 (xnor_5_out, entrada[1], in_1);
  not not_4 (not_6_out[2], xnor_4_out);
  not not_5 (not_6_out[1], xnor_5_out);
  xnor xnor_6 (xnor_6_out, entrada[0], in_1);
  not not_6 (not_6_out[0], xnor_6_out);

  // Other names for the same wires on the sheet: a = in_1; t0 = entrada[0]; t1 = entrada[1]; t2 = entrada[2];
  //   t3 = entrada[3]; t4 = entrada[4]

  // Notes on the sheet:
  //   entrada
  //   saída
endmodule

module Complemento2 (
  input  [5:0] entrada,
  input  Cpl,
  output Ts,
  output out_4,
  output out_5,
  output out_6,
  output out_7,
  output MSB,
  output LSB
);

  wire meiosomador_1_ts, meiosomador_2_ts, meiosomador_3_ts, meiosomador_4_ts, meiosomador_5_ts, xor_1_out,
       xor_2_out, xor_3_out, xor_4_out, xor_5_out, xor_6_out;

  xor xor_1 (xor_1_out, Cpl, entrada[0]);
  meiosomador meiosomador_1 (.A(xor_1_out), .B(Cpl), .s(LSB), .Ts(meiosomador_1_ts));
  xor xor_2 (xor_2_out, Cpl, entrada[1]);
  meiosomador meiosomador_2 (.A(xor_2_out), .B(meiosomador_1_ts), .s(out_4), .Ts(meiosomador_2_ts));
  xor xor_3 (xor_3_out, Cpl, entrada[2]);
  meiosomador meiosomador_3 (.A(xor_3_out), .B(meiosomador_2_ts), .s(out_5), .Ts(meiosomador_3_ts));
  xor xor_4 (xor_4_out, Cpl, entrada[3]);
  meiosomador meiosomador_4 (.A(xor_4_out), .B(meiosomador_3_ts), .s(out_6), .Ts(meiosomador_4_ts));
  xor xor_5 (xor_5_out, Cpl, entrada[4]);
  meiosomador meiosomador_5 (.A(xor_5_out), .B(meiosomador_4_ts), .s(out_7), .Ts(meiosomador_5_ts));
  xor xor_6 (xor_6_out, Cpl, entrada[5]);
  meiosomador meiosomador_6 (.A(xor_6_out), .B(meiosomador_5_ts), .s(MSB), .Ts(Ts));
  _7_Segment_Display u_7_segment_display_1 (.g(MSB));  // open: f, a, b, e, d, c, dp
  Hex_Digit_Display hex_digit_display_1 (.value({2'b00, entrada[5:4]}));  // open: dp
  Hex_Digit_Display hex_digit_display_2 (.value(entrada[3:0]));  // open: dp

  // Other names for the same wires on the sheet: display0cpl[3:0] = entrada[3:0]; display1cpl[1:0] = entrada[5:4]
endmodule

module teste_c2 (
  input  [5:0] in_1,
  input  in_2,
  output out_3,
  output out_4,
  output out_5,
  output out_6,
  output out_7,
  output out_8
);

  Complemento2 complemento2_1 (
    .entrada(in_1), .MSB(out_8), .Cpl(in_2), .out_7(out_7), .out_6(out_6), .out_5(out_5), .out_4(out_4),
    .LSB(out_3));  // open: Ts
endmodule
